# Fritzing sketch BLEcontroller_connected (saved by Fritzing 0.9.3b)
breadboards: 1

parts:
  U1_Left_+_motor = RELAY [package=relay-jzc]
  U2_Left_+_control = RELAY [package=relay-jzc]
  U3_Right_+_control = RELAY [package=relay-jzc]
  U4_Right_+_motor = RELAY [package=relay-jzc]
  U5_Brake = RELAY [package=relay-jzc]
  U6_Throttle = RELAY [package=relay-jzc]
  U7_Positive_Cut = RELAY [package=relay-jzc]
  U8_Positive_source = RELAY [package=relay-jzc]
  U9 = RELAY [package=relay-jzc]
  U10 = RELAY [package=relay-jzc]
  U11 = RELAY [package=relay-jzc]
  U12_Negative_cut = RELAY [package=relay-jzc]
  U13_Left_-_motor = RELAY [package=relay-jzc]
  U14_Left_-_control = RELAY [package=relay-jzc]
  U15_Right_-_control = RELAY [package=relay-jzc]
  U16_Right_-_motor = RELAY [package=relay-jzc]
  Q1 = NPN-Transistor [part_number=2N2222S package="TO92 [THT]"]
  R1 = Resistor [tolerance=±5% resistance=100k package=THT]
  Q2 = NPN-Transistor [part_number=2N2222S package="TO92 [THT]"]
  R2 = Resistor [tolerance=±5% resistance=100k package=THT]
  Q3 = NPN-Transistor [part_number=2N2222S package="TO92 [THT]"]
  Q4 = NPN-Transistor [part_number=2N2222S package="TO92 [THT]"]
  R3 = Resistor [tolerance=±5% resistance=100k package=THT]
  R4 = Resistor [tolerance=±5% resistance=100k package=THT]
  Q5 = NPN-Transistor [part_number=2N2222S package="TO92 [THT]"]
  Q6 = NPN-Transistor [part_number=2N2222S package="TO92 [THT]"]
  Q7 = NPN-Transistor [part_number=2N2222S package="TO92 [THT]"]
  Q8 = NPN-Transistor [part_number=2N2222S package="TO92 [THT]"]
  R5 = Resistor [tolerance=±5% resistance=100k package=THT]
  R6 = Resistor [tolerance=±5% resistance=100k package=THT]
  R7 = Resistor [tolerance=±5% resistance=100k package=THT]
  R8 = Resistor [tolerance=±5% resistance=100k package=THT]
  Q9 = NPN-Transistor [part_number=2N2222S package="TO92 [THT]"]
  Q10 = NPN-Transistor [part_number=2N2222S package="TO92 [THT]"]
  Q11 = NPN-Transistor [part_number=2N2222S package="TO92 [THT]"]
  Q12 = NPN-Transistor [part_number=2N2222S package="TO92 [THT]"]
  Q13 = NPN-Transistor [part_number=2N2222S package="TO92 [THT]"]
  Q14 = NPN-Transistor [part_number=2N2222S package="TO92 [THT]"]
  Q15 = NPN-Transistor [part_number=2N2222S package="TO92 [THT]"]
  Q16 = NPN-Transistor [part_number=2N2222S package="TO92 [THT]"]
  R9 = Resistor [tolerance=±5% resistance=100k package=THT]
  R10 = Resistor [tolerance=±5% resistance=100k package=THT]
  R11 = Resistor [tolerance=±5% resistance=100k package=THT]
  R12 = Resistor [tolerance=±5% resistance=100k package=THT]
  R13 = Resistor [tolerance=±5% resistance=100k package=THT]
  R14 = Resistor [tolerance=±5% resistance=100k package=THT]
  R15 = Resistor [tolerance=±5% resistance=100k package=THT]
  R16 = Resistor [tolerance=±5% resistance=100k package=THT]
  IC1 = Voltage Regulator [package=to-220-alt]
  VCC1 = Battery block 9V
  Part1 = Arduino Uno (Rev3) [part_number="Arduino 101"]
  Fuse3 = Fuse with Handler [part_number=Htc-15m]
  Throttle = Toggle Switch [package=THT]
  Brake = Toggle Switch [package=THT]
  12V_Batt = Battery Holders [package=battery-aa-panel]
  Right = DC Motor
  Left = DC Motor

nets:
  N1: U1_Left_+_motor.COIL2, U2_Left_+_control.COIL2, U16_Right_-_motor.COIL1
  Left +/Shifter L+: U1_Left_+_motor.NC
  N2: U1_Left_+_motor.NO, U2_Left_+_control.MAIN
  Left + motor lead: U1_Left_+_motor.MAIN, Left.pin_1
  N3: U1_Left_+_motor.COIL1, Q1.C
  N4: U2_Left_+_control.NC, U15_Right_-_control.NC
  N5: U2_Left_+_control.NO, U3_Right_+_control.NC, U5_Brake.MAIN, U14_Left_-_control.NO
  N6: U2_Left_+_control.COIL1, Q2.C
  N7: U3_Right_+_control.COIL2, U15_Right_-_control.COIL1
  N8: U3_Right_+_control.NO, U12_Negative_cut.NO, U14_Left_-_control.NC, U15_Right_-_control.NO
  N9: U3_Right_+_control.MAIN, U4_Right_+_motor.NO
  N10: U3_Right_+_control.COIL1, Q3.C
  N11: U4_Right_+_motor.COIL2, U14_Left_-_control.COIL1
  Right +/Shifter R+: U4_Right_+_motor.NC
  Rigth + motor lead: U4_Right_+_motor.MAIN, Right.pin_1
  N12: U4_Right_+_motor.COIL1, Q4.C
  N13: U5_Brake.COIL2, U13_Left_-_motor.COIL1
  Battery negative: U5_Brake.NC, U12_Negative_cut.MAIN, Fuse3.Connector2, Brake.L1
  N14: U5_Brake.NO, U6_Throttle.MAIN
  N15: U5_Brake.COIL1, Q5.C
  N16: U6_Throttle.COIL2, U12_Negative_cut.COIL1
  N17: U6_Throttle.NO, U7_Positive_Cut.NO
  N18: U6_Throttle.COIL1, Q7.C
  N19: U7_Positive_Cut.COIL2, U11.COIL1
  Positive/Shifter Positive: U7_Positive_Cut.NC
  N20: U7_Positive_Cut.MAIN, U8_Positive_source.MAIN
  N21: U7_Positive_Cut.COIL1, Q6.C
  N22: U8_Positive_source.COIL2, U9.COIL1, U10.COIL1, IC1.OUT
  Brake switch outout: U8_Positive_source.NC, Brake.COM
  Battery positive: U8_Positive_source.NO, Throttle.L2, 12V_Batt.+
  N23: U8_Positive_source.COIL1, Q8.C
  N24: U9.COIL2, Q9.C
  N25: U10.COIL2, Q10.C
  N26: U11.COIL2, Q11.C
  N27: U12_Negative_cut.COIL2, Q15.C
  Negative/Shifter negative: U12_Negative_cut.NC
  N28: U13_Left_-_motor.COIL2, Q13.C
  Left -/Shifter L-: U13_Left_-_motor.NC
  N29: U13_Left_-_motor.NO, U14_Left_-_control.MAIN
  Left - motor lead: U13_Left_-_motor.MAIN, Left.pin_2
  N30: U14_Left_-_control.COIL2, Q14.C
  N31: U15_Right_-_control.COIL2, Q16.C
  N32: U15_Right_-_control.MAIN, U16_Right_-_motor.NO
  N33: U16_Right_-_motor.COIL2, Q12.C
  Right -/Shifter R-: U16_Right_-_motor.NC
  Right - motor lead: U16_Right_-_motor.MAIN, Right.pin_2
  GND: Q1.E, Q2.E, Q3.E, Q4.E, Q5.E, Q6.E, Q7.E, Q8.E, Q9.E, Q10.E, Q11.E, Q12.E, Q13.E, Q14.E, Q15.E, Q16.E, IC1.GND, VCC1.-, Part1.GND
  N34: Q1.B, R1.Pin_1
  N35: R1.Pin_0, Part1.D0/RX
  N36: Q2.B, R2.Pin_1
  N37: R2.Pin_0, Part1.D1/TX
  N38: Q3.B, R3.Pin_1
  N39: Q4.B, R4.Pin_1
  N40: R3.Pin_0, Part1.D2
  N41: R4.Pin_0, Part1.D3_PWM
  N42: Q5.B, R5.Pin_1
  N43: Q6.B, R6.Pin_1
  N44: Q7.B, R8.Pin_1
  N45: Q8.B, R7.Pin_1
  N46: R5.Pin_0, Part1.D4
  N47: R6.Pin_0, Part1.D6_PWM
  N48: R7.Pin_0, Part1.D7
  N49: R8.Pin_0, Part1.D5_PWM
  N50: Q9.B, R9.Pin_1
  N51: Q10.B, R15.Pin_1
  N52: Q11.B, R12.Pin_1
  N53: Q12.B, R13.Pin_1
  N54: Q13.B, R14.Pin_1
  N55: Q14.B, R11.Pin_1
  N56: Q15.B, R10.Pin_1
  N57: Q16.B, R16.Pin_1
  N58: R9.Pin_0, Part1.D8
  N59: R10.Pin_0, Part1.D11_PWM/MOSI
  N60: R11.Pin_0, Part1.D13/SCK
  N61: R12.Pin_0, Part1.D10_PWM/SS
  N62: R13.Pin_0, Part1.A1
  N63: R14.Pin_0, Part1.D12/MISO
  N64: R15.Pin_0, Part1.D9_PWM
  N65: R16.Pin_0, Part1.A0
  +12vdc: IC1.IN
  N66: VCC1.+, Part1.VIN
  N67: Fuse3.Connector1, 12V_Batt.-
  N68: Throttle.COM, Brake.L2

notes:
  SainSmart Relay Module
  Shifter
