# Fritzing sketch BLEcontroller_v1 (saved by Fritzing 0.9.3b)
breadboards: 1

parts:
  U1 = RELAY [package=relay-jzc]
  U2 = RELAY [package=relay-jzc]
  U3 = RELAY [package=relay-jzc]
  U4 = RELAY [package=relay-jzc]
  U5 = RELAY [package=relay-jzc]
  U6 = RELAY [package=relay-jzc]
  U7 = RELAY [package=relay-jzc]
  U8 = RELAY [package=relay-jzc]
  U9 = RELAY [package=relay-jzc]
  U10 = RELAY [package=relay-jzc]
  U11 = RELAY [package=relay-jzc]
  U12 = RELAY [package=relay-jzc]
  U13 = RELAY [package=relay-jzc]
  U14 = RELAY [package=relay-jzc]
  U15 = RELAY [package=relay-jzc]
  U16 = RELAY [package=relay-jzc]
  Q1 = NPN-Transistor [part_number=2N2222S package="TO92 [THT]"]
  R1 = Resistor [tolerance=±5% resistance=100k package=THT]
  Q2 = NPN-Transistor [part_number=2N2222S package="TO92 [THT]"]
  R2 = Resistor [tolerance=±5% resistance=100k package=THT]
  Q3 = NPN-Transistor [part_number=2N2222S package="TO92 [THT]"]
  Q4 = NPN-Transistor [part_number=2N2222S package="TO92 [THT]"]
  R3 = Resistor [tolerance=±5% resistance=100k package=THT]
  R4 = Resistor [tolerance=±5% resistance=100k package=THT]
  Q5 = NPN-Transistor [part_number=2N2222S package="TO92 [THT]"]
  Q6 = NPN-Transistor [part_number=2N2222S package="TO92 [THT]"]
  Q7 = NPN-Transistor [part_number=2N2222S package="TO92 [THT]"]
  Q8 = NPN-Transistor [part_number=2N2222S package="TO92 [THT]"]
  R5 = Resistor [tolerance=±5% resistance=100k package=THT]
  R6 = Resistor [tolerance=±5% resistance=100k package=THT]
  R7 = Resistor [tolerance=±5% resistance=100k package=THT]
  R8 = Resistor [tolerance=±5% resistance=100k package=THT]
  Q9 = NPN-Transistor [part_number=2N2222S package="TO92 [THT]"]
  Q10 = NPN-Transistor [part_number=2N2222S package="TO92 [THT]"]
  Q11 = NPN-Transistor [part_number=2N2222S package="TO92 [THT]"]
  Q12 = NPN-Transistor [part_number=2N2222S package="TO92 [THT]"]
  Q13 = NPN-Transistor [part_number=2N2222S package="TO92 [THT]"]
  Q14 = NPN-Transistor [part_number=2N2222S package="TO92 [THT]"]
  Q15 = NPN-Transistor [part_number=2N2222S package="TO92 [THT]"]
  Q16 = NPN-Transistor [part_number=2N2222S package="TO92 [THT]"]
  R9 = Resistor [tolerance=±5% resistance=100k package=THT]
  R10 = Resistor [tolerance=±5% resistance=100k package=THT]
  R11 = Resistor [tolerance=±5% resistance=100k package=THT]
  R12 = Resistor [tolerance=±5% resistance=100k package=THT]
  R13 = Resistor [tolerance=±5% resistance=100k package=THT]
  R14 = Resistor [tolerance=±5% resistance=100k package=THT]
  R15 = Resistor [tolerance=±5% resistance=100k package=THT]
  R16 = Resistor [tolerance=±5% resistance=100k package=THT]
  IC1 = Voltage Regulator [package=to-220-alt]
  VCC1 = Battery block 9V
  Part1 = Arduino Uno (Rev3) [part_number="Arduino 101"]

nets:
  N1: U1.COIL2, U2.COIL2, U16.COIL1
  Shifter L+: U1.NC
  N2: U1.NO, U2.MAIN
  Left + motor lead: U1.MAIN
  N3: U1.COIL1, Q1.C
  N4: U2.NC, U15.NC
  N5: U2.NO, U3.NC, U5.MAIN, U14.NO
  N6: U2.COIL1, Q2.C
  N7: U3.COIL2, U15.COIL1
  N8: U3.NO, U12.NO, U14.NC, U15.NO
  N9: U3.MAIN, U4.NO
  N10: U3.COIL1, Q3.C
  N11: U4.COIL2, U14.COIL1
  Shifter R+: U4.NC
  Rigth + motor lead: U4.MAIN
  N12: U4.COIL1, Q4.C
  N13: U5.COIL2, U13.COIL1
  Battery negative: U5.NC, U12.MAIN
  N14: U5.NO, U6.MAIN
  N15: U5.COIL1, Q5.C
  N16: U6.COIL2, U12.COIL1
  N17: U6.NO, U7.NO
  N18: U6.COIL1, Q7.C
  N19: U7.COIL2, U11.COIL1
  Throttle switch input: U7.NC
  N20: U7.MAIN, U8.MAIN
  N21: U7.COIL1, Q6.C
  N22: U8.COIL2, U9.COIL1, U10.COIL1, IC1.OUT
  Battery positive: U8.NC
  Brake switch outout: U8.NO
  N23: U8.COIL1, Q8.C
  N24: U9.COIL2, Q9.C
  N25: U10.COIL2, Q10.C
  N26: U11.COIL2, Q11.C
  N27: U12.COIL2, Q15.C
  Shifter negative: U12.NC
  N28: U13.COIL2, Q13.C
  Shifter L-: U13.NC
  N29: U13.NO, U14.MAIN
  Left - motor lead: U13.MAIN
  N30: U14.COIL2, Q14.C
  N31: U15.COIL2, Q16.C
  N32: U15.MAIN, U16.NO
  N33: U16.COIL2, Q12.C
  Shifter R-: U16.NC
  Right - motor lead: U16.MAIN
  GND: Q1.E, Q2.E, Q3.E, Q4.E, Q5.E, Q6.E, Q7.E, Q8.E, Q9.E, Q10.E, Q11.E, Q12.E, Q13.E, Q14.E, Q15.E, Q16.E, IC1.GND, VCC1.-, Part1.GND
  N34: Q1.B, R1.Pin_1
  N35: R1.Pin_0, Part1.D0/RX
  N36: Q2.B, R2.Pin_1
  N37: R2.Pin_0, Part1.D1/TX
  N38: Q3.B, R3.Pin_1
  N39: Q4.B, R4.Pin_1
  N40: R3.Pin_0, Part1.D2
  N41: R4.Pin_0, Part1.D3_PWM
  N42: Q5.B, R5.Pin_1
  N43: Q6.B, R6.Pin_1
  N44: Q7.B, R8.Pin_1
  N45: Q8.B, R7.Pin_1
  N46: R5.Pin_0, Part1.D4
  N47: R6.Pin_0, Part1.D6_PWM
  N48: R7.Pin_0, Part1.D7
  N49: R8.Pin_0, Part1.D5_PWM
  N50: Q9.B, R9.Pin_1
  N51: Q10.B, R15.Pin_1
  N52: Q11.B, R12.Pin_1
  N53: Q12.B, R13.Pin_1
  N54: Q13.B, R14.Pin_1
  N55: Q14.B, R11.Pin_1
  N56: Q15.B, R10.Pin_1
  N57: Q16.B, R16.Pin_1
  N58: R9.Pin_0, Part1.D8
  N59: R10.Pin_0, Part1.D11_PWM/MOSI
  N60: R11.Pin_0, Part1.D13/SCK
  N61: R12.Pin_0, Part1.D10_PWM/SS
  N62: R13.Pin_0, Part1.A1
  N63: R14.Pin_0, Part1.D12/MISO
  N64: R15.Pin_0, Part1.D9_PWM
  N65: R16.Pin_0, Part1.A0
  +12vdc: IC1.IN
  N66: VCC1.+, Part1.VIN

notes:
  SainSmart Relay Module
