# Fritzing sketch PerPeregoShifter expanded (saved by Fritzing 0.9.3b)

parts:
  Fuse1 = Fuse with Handler [part_number=Htc-15m]
  Brake = Toggle Switch [package=THT]
  12V_Batt = Battery Holders [package=battery-aa-panel]
  Throttle = Toggle Switch [package=THT]
  Right = DC Motor
  Left = DC Motor
  low/high_speed = SWITCH-DPDT [package=os]
  forward/reverse = SWITCH-DPDT [package=os]

nets:
  N1: Fuse1.Connector1, 12V_Batt.-
  N2: Fuse1.Connector2, Brake.L1, low/high_speed.3, forward/reverse.1, forward/reverse.6
  N3: Brake.COM, low/high_speed.6, forward/reverse.3, forward/reverse.4
  N4: Brake.L2, Throttle.COM
  N5: 12V_Batt.+, Throttle.L2
  N6: Right.pin_1, forward/reverse.5
  N7: Right.pin_2, low/high_speed.2
  N8: Left.pin_1, low/high_speed.5
  N9: Left.pin_2, forward/reverse.2
  N10: low/high_speed.1, low/high_speed.4
