# Fritzing sketch PerPeregoShifter (saved by Fritzing 0.9.3b)

parts:
  Fuse1 = Fuse with Handler [part_number=Htc-15m]
  Brake = Toggle Switch [package=THT]
  12v_Batt = Battery Holders [package=battery-aa-panel]
  Throttle = Toggle Switch [package=THT]
  Right = DC Motor
  Left = DC Motor

nets:
  N1: Fuse1.Connector1, 12v_Batt.-
  Negative: Fuse1.Connector2, Brake.L1
  Positive: Brake.COM
  N2: Brake.L2, Throttle.COM
  N3: 12v_Batt.+, Throttle.L2
  Right +: Right.pin_1
  Right -: Right.pin_2
  Left +: Left.pin_1
  Left -: Left.pin_2

notes:
  Shifter
